# Fritzing sketch SumSchematic (saved by Fritzing 0.9.3b)
breadboards: 1

parts:
  Raspberry_Pi_1 = Raspberry Pi 3 [part_number=RPI-3-V1.2]
  Down_Button = Pushbutton [package="[THT]"]
  R1 = Resistor [tolerance=±5% resistance=10k package="0805 [SMD]"]
  Up_Button = Pushbutton [package="[THT]"]
  R2 = Resistor [tolerance=±5% resistance=10k package="0805 [SMD]"]
  Start_Button = Pushbutton [package="[THT]"]
  R3 = Resistor [tolerance=±5% resistance=10k package="0805 [SMD]"]
  End_Button = Pushbutton [package="[THT]"]
  R4 = Resistor [tolerance=±5% resistance=10k package="0805 [SMD]"]
  Missile_Button = Pushbutton [package="[THT]"]
  R5 = Resistor [tolerance=±5% resistance=10k package="0805 [SMD]"]

nets:
  N1: Raspberry_Pi_1.GND, R1.Pin_1, R2.Pin_1, R3.Pin_1, R4.Pin_1, R5.Pin_1
  N2: Raspberry_Pi_1.GIPO24, Raspberry_Pi_1.GIPO23, Raspberry_Pi_1.GIPO18, Raspberry_Pi_1.GIPO15, Raspberry_Pi_1.GIPO14, Raspberry_Pi_1.5V, Down_Button.Pin_3, Down_Button.Pin_4, Up_Button.Pin_3, Up_Button.Pin_4, Start_Button.Pin_3, Start_Button.Pin_4, End_Button.Pin_3, End_Button.Pin_4, Missile_Button.Pin_3, Missile_Button.Pin_4
  N3: Down_Button.Pin_2, R1.Pin_0
  N4: Up_Button.Pin_1, Up_Button.Pin_2, R2.Pin_0
  N5: Start_Button.Pin_1, Start_Button.Pin_2, R3.Pin_0
  N6: End_Button.Pin_1, End_Button.Pin_2, R4.Pin_0
  N7: Missile_Button.Pin_1, Missile_Button.Pin_2, R5.Pin_0
