# Fritzing sketch Wiring Diagram (saved by Fritzing 0.9.3b)
breadboards: 1

parts:
  Down_Button = Pushbutton [package="[SMD]"]
  End_Button = Pushbutton [package="[SMD]"]
  R2 = Resistor [tolerance=±5% resistance=10k package="0603 [SMD]"]
  R1 = Resistor [tolerance=±5% resistance=10k package="2010 [SMD]"]
  R7 = Resistor [tolerance=±5% resistance=10k package="2010 [SMD]"]
  Missile_Button = Pushbutton [package="[SMD]"]
  Start_Button = Pushbutton [package="[SMD]"]
  Up_Button = Pushbutton [package="[SMD]"]
  Raspberry_Pi_1 = Raspberry Pi 3 [part_number=RPI-3-V1.2]
  R8 = Resistor [tolerance=±5% resistance=10k package="0603 [SMD]"]
  R9 = Resistor [tolerance=±5% resistance=10k package="0603 [SMD]"]

nets:
  N1: Down_Button.Pin_1, Down_Button.Pin_2, End_Button.Pin_1, End_Button.Pin_2, Missile_Button.Pin_1, Missile_Button.Pin_2, Start_Button.Pin_1, Start_Button.Pin_2, Up_Button.Pin_1, Up_Button.Pin_2, Raspberry_Pi_1.5V
  N2: Down_Button.Pin_3, Down_Button.Pin_4, R1.Pin_0, Raspberry_Pi_1.GIPO14
  N3: End_Button.Pin_3, End_Button.Pin_4, Raspberry_Pi_1.GIPO23, R9.Pin_0
  N4: R2.Pin_0, Up_Button.Pin_3, Up_Button.Pin_4, Raspberry_Pi_1.GIPO15
  N5: R2.Pin_1, R1.Pin_1, R7.Pin_1, Raspberry_Pi_1.GND, R8.Pin_1, R9.Pin_1
  N6: R7.Pin_0, Missile_Button.Pin_3, Missile_Button.Pin_4, Raspberry_Pi_1.GIPO24
  N7: Start_Button.Pin_3, Start_Button.Pin_4, Raspberry_Pi_1.GIPO18, R8.Pin_0
